# Fritzing sketch frtizing sketch (saved by Fritzing 0.9.2b)

parts:
  PART1 = SparkFun Soil Moisture Sensor [part_number=SEN-13322]
  KY-1 = Keyes Relay [package=THT]
  Parte1 = Arduino Uno (Rev3)
  Parte1_2 = Arduino Uno (Rev3) - ICSP
  M1 = DC Motor
  VCC1 = Battery

nets:
  N1: PART1.VCC, Parte1.D8, Parte1_2.D8
  GND: PART1.GND, KY-1.ground, Parte1.GND, Parte1_2.GND
  N2: PART1.SIG, Parte1.A0, Parte1_2.A0
  N3: KY-1.signal, Parte1.D7, Parte1_2.D7
  5V: KY-1.power, Parte1.5V, Parte1_2.5V
  N4: KY-1.NC, VCC1.-
  N5: KY-1.C, M1.pin_2

custom parts:
  SparkFun Soil Moisture Sensor: The SparkFun Soil Moisture Sensor is a simple breakout for measuring the moisture in soil and similar materials.
  Keyes Relay: The Keyes 5V relay module is suitable for SCM development, home appliance control. It uses a 5V~12V TIL control signal which can control DC / AC signal.

// code stored in the sketch: sketch.ino
//declare pinout
int pinSensor = A0;
int pinPower = 8;
int pinRelay = 7;
int measured = 0;
int minMoisture = 0;
int maxMoisture = 0;
int waitTimeStopped = 3600000; //one hour
int waitTImeRunning = 5000; //five seconds

void setup() 
{
	pinMode(pinPower, OUTPUT);//set pinPower as OUTPUT
	pinMode(pinRelay, OUTPUT);//set pinRelay as OUTPUT
  digitalWrite(soilPower, LOW);//set pinPower to LOW in order to shutdown the sensor
	digitalWrite(pinRelay, LOW);//set pinRelay to low in order to shutdown the water pump
}

void loop() 
{
	readSensor();//read the moisture level
	if(measured <= minMoisture)//if it is lower than the requested start to irrigate
	{
		//while the moisture level is under the max level requested, it will start the pump, and check
		//each ten seconds, when the moisture is over the moisture requested it will stop the pump and
		//recheck each ten minutes
		digitalWrite(pinRelay, HIGH);
		while(measured < maxMoisture)
		{
			delay(waitTImeRunning)//wait ten seconds
			readSensor();//read the sensor value
		}
		digitalWrite(pinRelay, LOW);//stop the water pump
	}
	delay(waitTimeStopped)// wait ten minutes
}

void readSensor()
{
	digitalWrite(soilPower, HIGH);//turn on the sensor
	delay(10);//wait to the sensor becomes stable
	measured = digitalRead(pinSensor);//store the data
	digitalWrite(soilPower, LOW);//turn off the sensor
}
